// Logisim project ALU.circ as structural Verilog: 1 circuit, main circuit ALU
module ALU (
  input  [4:0] in_1,
  input  [31:0] in_2,
  input  [31:0] A,
  input  [31:0] B,
  input  [4:0] Shift,
  input  CarryIn,
  input  [3:0] Codop,
  input  [4:0] in_8,
  input  [4:0] in_9,
  input  in_10,
  input  in_11,
  input  [4:0] in_12,
  input  [4:0] in_13,
  input  [4:0] in_14,
  input  [4:0] in_15,
  input  [4:0] in_16,
  output [31:0] S,
  output [3:0] Flags
);

  wire ADC, and_3_out, and_4_out, and_5_out, and_6_out, and_7_out, and_8_out, and_9_out, and_10_out,
       bitselector_1_out, bitselector_2_out, bitselector_3_out, bitselector_4_out, bitselector_5_out,
       bitselector_6_out, bitselector_7_out, bitselector_8_out, bitselector_12_out, CMN, CMP, not_2_out,
       not_3_out, not_4_out, not_5_out, not_6_out, not_7_out, not_8_out, not_9_out, not_10_out, not_11_out,
       not_12_out, not_13_out, not_14_out, or_2_out, or_3_out, or_4_out, or_5_out, SBC;
  wire [1:0] comparator_1_eq, comparator_2_eq, comparator_3_eq, comparator_4_eq;
  wire [4:0] negator_2_out, subtractor_2_out, subtractor_3_out;
  wire [31:0] adder_1_out, and_2_out, ET, multiplier_1_out, negator_1_out, not_1_out, or_1_out, RCMN, RCMP,
       shifter_1_out, shifter_2_out, shifter_3_out, shifter_4_out, subtractor_1_out, xor_1_out;

  assign xor_1_out = A ^ B;  // XOR_Gate xor_1, 32 bits wide
  assign not_1_out = ~B;  // NOT_Gate not_1, 32 bits wide
  assign ET = A & B;  // AND_Gate and_1, 32 bits wide
  Shifter #(.width(32)) shifter_1 (.in(B), .\dist (Shift), .out(shifter_1_out));
  Shifter #(.shift("lr"), .width(32)) shifter_2 (.in(B), .\dist (Shift), .out(shifter_2_out));
  Shifter #(.shift("ar"), .width(32)) shifter_3 (.in(B), .\dist (Shift), .out(shifter_3_out));
  Adder #(.width(32)) adder_1 (.a(A), .b(B), .out(adder_1_out), .cin(CarryIn), .cout(ADC));
  not not_2 (not_2_out, CarryIn);
  Subtractor #(.width(32)) subtractor_1 (.a(A), .b(B), .out(subtractor_1_out), .bin(not_2_out), .bout(SBC));
  Shifter #(.shift("rr"), .width(32)) shifter_4 (.in(B), .\dist (Shift), .out(shifter_4_out));
  Negator #(.width(32)) negator_1 (.in(A), .out(negator_1_out));
  assign or_1_out = A | B;  // OR_Gate or_1, 32 bits wide
  Multiplier #(.width(32)) multiplier_1 (.a(A), .b(B), .out(multiplier_1_out));  // open: cin, cout
  assign and_2_out = A & not_1_out;  // AND_Gate and_2, 32 bits wide
  BitSelector #(.width(32)) bitselector_1 (.in(S), .out(bitselector_1_out), .sel(in_9));
  Negator #(.width(5)) negator_2 (.in(Shift), .out(negator_2_out));
  Subtractor #(.width(5)) subtractor_2 (.a(Shift), .b(in_8), .out(subtractor_2_out));  // open: bin, bout
  Subtractor #(.width(5)) subtractor_3 (.a(Shift), .b(in_8), .out(subtractor_3_out));  // open: bin, bout
  BitSelector #(.width(32)) bitselector_2 (.in(S), .out(bitselector_2_out), .sel(negator_2_out));
  BitSelector #(.width(32)) bitselector_3 (.in(S), .out(bitselector_3_out), .sel(subtractor_2_out));
  BitSelector #(.width(32)) bitselector_4 (.in(S), .out(bitselector_4_out), .sel(subtractor_3_out));
  Multiplexer #(.enable("false"), .select(4), .width(32)) multiplexer_1 (
    .in0(ET), .in1(xor_1_out), .in2(shifter_1_out), .in3(shifter_2_out), .in4(shifter_3_out),
    .in5(adder_1_out), .in6(subtractor_1_out), .in7(shifter_4_out), .in8(B), .in9(negator_1_out), .in10(B),
    .in11(B), .in12(or_1_out), .in13(multiplier_1_out), .in14(and_2_out), .in15(not_1_out), .out(S),
    .sel(Codop));
  Multiplexer #(.enable("false"), .select(4)) multiplexer_2 (
    .in0(in_10), .in1(in_10), .in2(bitselector_2_out), .in3(bitselector_3_out), .in4(bitselector_4_out),
    .in5(ADC), .in6(SBC), .in7(bitselector_1_out), .in8(in_10), .in9(in_10), .in10(CMP), .in11(CMN),
    .in12(in_10), .in13(in_10), .in14(in_10), .in15(in_10), .out(Flags[1]), .sel(Codop));
  BitSelector #(.width(32)) bitselector_5 (.in(RCMN), .out(bitselector_5_out), .sel(in_12));
  BitSelector #(.width(32)) bitselector_6 (.in(RCMP), .out(bitselector_6_out), .sel(in_13));
  BitSelector #(.width(32)) bitselector_7 (.in(S), .out(bitselector_7_out), .sel(in_14));
  Comparator #(.width(32)) comparator_1 (.a(S), .b(in_2), .eq(comparator_1_eq[0]));  // open: gt, lt
  Subtractor #(.width(32)) subtractor_4 (.a(A), .b(B), .out(RCMP), .bout(CMP));  // open: bin
  Adder #(.width(32)) adder_2 (.a(A), .b(B), .out(RCMN), .cout(CMN));  // open: cin
  BitSelector #(.width(32)) bitselector_8 (.in(B), .out(bitselector_8_out), .sel(in_15));
  BitSelector #(.width(32)) bitselector_9 (.in(ET), .out(comparator_2_eq[1]), .sel(in_1));
  Comparator #(.width(32)) comparator_2 (.a(in_2), .b(ET), .eq(comparator_2_eq[0]));  // open: gt, lt
  BitSelector #(.width(32)) bitselector_10 (.in(RCMP), .out(comparator_3_eq[1]), .sel(in_1));
  Comparator #(.width(32)) comparator_3 (.b(RCMP), .eq(comparator_3_eq[0]));  // open: a, gt, lt
  BitSelector #(.width(32)) bitselector_11 (.in(RCMN), .out(comparator_4_eq[1]), .sel(in_1));
  Comparator #(.width(32)) comparator_4 (.b(RCMN), .eq(comparator_4_eq[0]));  // open: a, gt, lt
  BitSelector #(.width(32)) bitselector_12 (.in(A), .out(bitselector_12_out), .sel(in_16));
  BitSelector #(.width(32)) bitselector_13 (.in(S), .out(comparator_1_eq[1]), .sel(in_1));
  not not_3 (not_3_out, bitselector_12_out);
  not not_4 (not_4_out, bitselector_8_out);
  not not_5 (not_5_out, bitselector_7_out);
  not not_6 (not_6_out, bitselector_8_out);
  not not_7 (not_7_out, bitselector_7_out);
  not not_8 (not_8_out, bitselector_12_out);
  not not_9 (not_9_out, bitselector_6_out);
  not not_10 (not_10_out, bitselector_8_out);
  not not_11 (not_11_out, bitselector_12_out);
  not not_12 (not_12_out, bitselector_12_out);
  not not_13 (not_13_out, bitselector_8_out);
  not not_14 (not_14_out, bitselector_5_out);
  and and_3 (and_3_out, not_3_out, not_4_out, bitselector_7_out);
  and and_4 (and_4_out, not_5_out, bitselector_8_out, bitselector_12_out);
  and and_5 (and_5_out, bitselector_12_out, not_6_out, not_7_out);
  and and_6 (and_6_out, not_8_out, bitselector_8_out, bitselector_7_out);
  and and_7 (and_7_out, not_9_out, not_10_out, bitselector_12_out);
  and and_8 (and_8_out, not_11_out, bitselector_8_out, bitselector_6_out);
  and and_9 (and_9_out, bitselector_5_out, not_12_out, not_13_out);
  and and_10 (and_10_out, not_14_out, bitselector_8_out, bitselector_12_out);
  or or_2 (or_2_out, and_3_out, and_4_out);
  or or_3 (or_3_out, and_5_out, and_6_out);
  or or_4 (or_4_out, and_7_out, and_8_out);
  or or_5 (or_5_out, and_9_out, and_10_out);
  Multiplexer #(.enable("false"), .select(4), .width(2)) multiplexer_3 (
    .in0(comparator_1_eq), .in1(comparator_1_eq), .in2(comparator_1_eq), .in3(comparator_1_eq),
    .in4(comparator_1_eq), .in5(comparator_1_eq), .in6(comparator_1_eq), .in7(comparator_1_eq),
    .in8(comparator_2_eq), .in9(comparator_1_eq), .in10(comparator_3_eq), .in11(comparator_4_eq),
    .in12(comparator_1_eq), .in13(comparator_1_eq), .in14(comparator_1_eq), .in15(comparator_1_eq),
    .out(Flags[3:2]), .sel(Codop));
  Multiplexer #(.enable("false"), .select(4)) multiplexer_4 (
    .in0(in_11), .in1(in_11), .in2(in_11), .in3(in_11), .in4(in_11), .in5(or_2_out), .in6(or_3_out),
    .in7(in_11), .in8(in_11), .in9(in_11), .in10(or_4_out), .in11(or_5_out), .in12(in_11), .in13(in_11),
    .in14(in_11), .in15(in_11), .out(Flags[0]), .sel(Codop));

  // Other names for the same wires on the sheet: Cin = CarryIn; COPOD[3:0] = Codop; V = Flags[0]; C = Flags[1];
  //   NZ[1:0] = Flags[3:2]; Res[31:0] = S

  // Notes on the sheet:
  //   Note: for ROR, C = N
  //   Note 2: assume that shift > 0 for LSL and LSR
endmodule
