// Logisim project Ctl_Shift_Add_Sub_Mov.circ as structural Verilog: 2 circuits, main circuit Shift_Add_Sub_Mov
module Shift_Add_Sub_Mov (
  input  Enable,
  input  [15:0] Instruction,
  output [3:0] Flags_Update_Mask,
  output Carry,
  output Imm32_Enable,
  output [2:0] Rm,
  output [2:0] Rn,
  output [2:0] Rd,
  output [4:0] Imm5,
  output [31:0] Imm32,
  output [3:0] ALU_Opcode
);

  wire ADD3, ADD8, ADDR, ADDSUB3, and_13_out, and_15_out, and_16_out, and_17_out, and_18_out, and_19_out,
       and_27_out, and_28_out, and_29_out, ASL, B0, B1, B2, B3, B4, B5, B6, B7, B8, B9, B10, B11, B12, B13,
       B14, B15, CMP, LSL, LSR, MOVE, MOVE_CMP_8, not_1_out, not_2_out, not_3_out, not_4_out, not_5_out,
       not_6_out, not_7_out, not_8_out, not_9_out, not_10_out, not_11_out, not_12_out, not_13_out,
       not_14_out, not_15_out, not_16_out, not_17_out, not_18_out, not_19_out, or_5_out, or_6_out, or_8_out,
       or_13_out, REGI, SHIFT, SUB3, SUB8, SUBR;
  wire [2:0] and_21_out, and_23_out, and_24_out, and_30_out, and_31_out, bit_extender_3_out,
       bit_extender_4_out, bit_extender_6_out, bit_extender_7_out, bit_extender_13_out, bit_extender_14_out;
  wire [3:0] bit_extender_8_out, bit_extender_12_out, multiplexer_1_out, multiplexer_2_out,
       multiplexer_3_out, or_9_out, shift_to_opcode_1_s4;
  wire [4:0] bit_extender_2_out;
  wire [7:0] and_22_out, bit_extender_5_out, bit_extender_9_out, or_12_out;
  wire [15:0] bit_extender_1_out;
  wire [31:0] bit_extender_10_out, bit_extender_11_out, negator_1_out;

  not not_1 (not_1_out, B9);
  not not_2 (not_2_out, B10);
  not not_3 (not_3_out, B13);
  not not_4 (not_4_out, B10);
  not not_5 (not_5_out, B13);
  not not_6 (not_6_out, B9);
  not not_7 (not_7_out, B13);
  not not_8 (not_8_out, B13);
  not not_9 (not_9_out, B11);
  not not_10 (not_10_out, B12);
  not not_11 (not_11_out, B12);
  not not_12 (not_12_out, B11);
  assign bit_extender_1_out = {{15{Enable}}, Enable};  // Bit_Extender bit_extender_1
  assign {B15, B14, B13, B12, B11, B10, B9, B8, B7, B6, B5, B4, B3, B2, B1, B0} = Instruction & bit_extender_1_out;  // AND_Gate and_1, 16 bits wide
  not not_13 (not_13_out, B11);
  not not_14 (not_14_out, B12);
  not not_15 (not_15_out, B13);
  not not_16 (not_16_out, B12);
  not not_17 (not_17_out, B13);
  not not_18 (not_18_out, B11);
  not not_19 (not_19_out, B13);
  and and_2 (ADDR, not_1_out, not_2_out, B11, B12, not_3_out);
  and and_3 (SUBR, B9, not_4_out, B11, B12, not_5_out);
  and and_4 (ADD3, not_6_out, B10, B11, B12, not_7_out);
  and and_5 (SUB3, B9, B10, B11, B12, not_8_out);
  and and_6 (MOVE, not_9_out, not_10_out, B13);
  and and_7 (CMP, B11, not_11_out, B13);
  and and_8 (ADD8, not_12_out, B12, B13);
  and and_9 (SUB8, B11, B12, B13);
  and and_10 (LSL, not_13_out, not_14_out, not_15_out);
  and and_11 (LSR, B11, not_16_out, not_17_out);
  and and_12 (ASL, not_18_out, B12, not_19_out);
  or or_1 (SHIFT, LSL, LSR, ASL);
  and and_13 (and_13_out, Enable, SHIFT);
  or or_2 (REGI, ADDR, SUBR);
  or or_3 (ADDSUB3, ADD3, SUB3);
  or or_4 (MOVE_CMP_8, MOVE, CMP, ADD8, SUB8);
  Multiplexer #(.enable("false"), .width(4)) multiplexer_1 (
    .in0(4'b0000), .in1(4'b1111), .out(multiplexer_1_out), .sel(or_5_out));
  or or_5 (or_5_out, REGI, ADDSUB3, CMP, ADD8, SUB8);
  assign bit_extender_2_out = {{4{and_13_out}}, and_13_out};  // Bit_Extender bit_extender_2
  assign Imm5 = {B10, B9, B8, B7, B6} & bit_extender_2_out;  // AND_Gate and_14, 5 bits wide
  or or_6 (or_6_out, ASL, LSR, LSL);
  Multiplexer #(.enable("false"), .width(4)) multiplexer_2 (
    .in0(4'b0000), .in1(4'b1100), .out(multiplexer_2_out), .sel(MOVE));
  Multiplexer #(.enable("false"), .width(4)) multiplexer_3 (
    .in0(4'b0000), .in1(4'b1110), .out(multiplexer_3_out), .sel(or_6_out));
  or or_7 (Carry, SUB8, SUBR, SUB3);
  or or_8 (or_8_out, REGI, SHIFT, ADDSUB3);
  and and_15 (and_15_out, Enable, REGI);
  and and_16 (and_16_out, Enable, ADDSUB3);
  and and_17 (and_17_out, Enable, MOVE_CMP_8);
  and and_18 (and_18_out, Enable, or_8_out);
  and and_19 (and_19_out, Enable, MOVE_CMP_8);
  assign bit_extender_3_out = {{2{and_15_out}}, and_15_out};  // Bit_Extender bit_extender_3
  assign bit_extender_4_out = {{2{and_16_out}}, and_16_out};  // Bit_Extender bit_extender_4
  assign bit_extender_5_out = {{7{and_17_out}}, and_17_out};  // Bit_Extender bit_extender_5
  assign bit_extender_6_out = {{2{and_18_out}}, and_18_out};  // Bit_Extender bit_extender_6
  assign bit_extender_7_out = {{2{and_19_out}}, and_19_out};  // Bit_Extender bit_extender_7
  assign or_9_out = multiplexer_3_out | multiplexer_1_out | multiplexer_2_out;  // OR_Gate or_9, 4 bits wide
  assign bit_extender_8_out = {{3{Enable}}, Enable};  // Bit_Extender bit_extender_8
  assign Rm = {B8, B7, B6} & bit_extender_3_out;  // AND_Gate and_20, 3 bits wide
  assign and_21_out = {B8, B7, B6} & bit_extender_4_out;  // AND_Gate and_21, 3 bits wide
  assign and_22_out = {B7, B6, B5, B4, B3, B2, B1, B0} & bit_extender_5_out;  // AND_Gate and_22, 8 bits wide
  assign and_23_out = {B2, B1, B0} & bit_extender_6_out;  // AND_Gate and_23, 3 bits wide
  assign and_24_out = {B10, B9, B8} & bit_extender_7_out;  // AND_Gate and_24, 3 bits wide
  or or_10 (Imm32_Enable, ADD3, SUB3, SUB8, ADD8, MOVE, CMP);
  assign Flags_Update_Mask = or_9_out & bit_extender_8_out;  // AND_Gate and_25, 4 bits wide
  assign bit_extender_9_out = {{5{1'b0}}, and_21_out};  // Bit_Extender bit_extender_9
  assign Rd = and_23_out | and_24_out;  // OR_Gate or_11, 3 bits wide
  assign or_12_out = bit_extender_9_out | and_22_out;  // OR_Gate or_12, 8 bits wide
  assign bit_extender_10_out = {{24{1'b0}}, {B7, B6, B5, B4, B3, B2, B1, B0}};  // Bit_Extender bit_extender_10
  assign ALU_Opcode = shift_to_opcode_1_s4 & bit_extender_12_out;  // AND_Gate and_26, 4 bits wide
  Shift_To_Opcode shift_to_opcode_1 (
    .e1(B13), .e2(B12), .e3(B11), .e4(B10), .e5(B9), .s1(shift_to_opcode_1_s4[3]),
    .s2(shift_to_opcode_1_s4[2]), .s3(shift_to_opcode_1_s4[1]), .s4(shift_to_opcode_1_s4[0]));
  or or_13 (or_13_out, REGI, ADDSUB3);
  assign bit_extender_11_out = {{24{1'b0}}, or_12_out};  // Bit_Extender bit_extender_11
  Negator #(.width(32)) negator_1 (.in(bit_extender_10_out), .out(negator_1_out));
  assign bit_extender_12_out = {{3{Enable}}, Enable};  // Bit_Extender bit_extender_12
  assign bit_extender_13_out = {{2{and_27_out}}, and_27_out};  // Bit_Extender bit_extender_13
  and and_27 (and_27_out, Enable, or_13_out);
  assign bit_extender_14_out = {{2{and_28_out}}, and_28_out};  // Bit_Extender bit_extender_14
  and and_28 (and_28_out, Enable, SHIFT);
  and and_29 (and_29_out, MOVE, Enable);
  assign and_30_out = {B5, B4, B3} & bit_extender_13_out;  // AND_Gate and_30, 3 bits wide
  assign and_31_out = {B5, B4, B3} & bit_extender_14_out;  // AND_Gate and_31, 3 bits wide
  Multiplexer #(.enable("false"), .width(32)) multiplexer_4 (
    .in0(bit_extender_11_out), .in1(negator_1_out), .out(Imm32), .sel(and_29_out));
  assign Rn = and_30_out | and_31_out;  // OR_Gate or_14, 3 bits wide

  // Other names for the same wires on the sheet: FLAGS[3:0] = Flags_Update_Mask; IMM3[2:0] = {B8, B7, B6};
  //   IMM5_t[4:0] = {B10, B9, B8, B7, B6}; IMM8[7:0] = {B7, B6, B5, B4, B3, B2, B1, B0}; RM_REG_3[2:0] = {B8, B7, B6};
  //   RD_REG_3[2:0] = {B2, B1, B0}; RD_SHIFT[2:0] = {B2, B1, B0}; RM_SHIFT[2:0] = {B5, B4, B3};
  //   RN_REG[2:0] = {B5, B4, B3}; IMM_ENABLE = Imm32_Enable; Op_code[3:0] = ALU_Opcode;
  //   RD_MV_CMP_8[2:0] = {B10, B9, B8}

  // Notes on the sheet:
  //   Pull output low on Enable = 0
  //   only ADD and SUB use Rm
  //   Enable carry for SUB since it is reversed in ALU
  //   ALU will use Imm32 instead of Rm
  //   Note 3: Imm32_Enable forces the use of the immediate for Rm register
  //   Note: ALU uses Rn register for shifts. Use Rn instead of Rm for shifts (immediate) here too
  //   Note 2: MOV uses RSB ALU opcode with Imm8 reversed so that it is copied to output register
endmodule

module Shift_To_Opcode (
  input  e1,
  input  e2,
  input  e3,
  input  e4,
  input  e5,
  output s1,
  output s2,
  output s3,
  output s4
);

  wire and_2_out, and_3_out, and_4_out, and_5_out, and_6_out, and_7_out, not_1_out, not_2_out, not_3_out,
       not_4_out;

  not not_1 (not_1_out, e1);
  not not_2 (not_2_out, e2);
  not not_3 (not_3_out, e3);
  not not_4 (not_4_out, e5);
  and and_1 (s1, e1, not_2_out);
  and and_2 (and_2_out, not_1_out, not_2_out);
  and and_3 (and_3_out, e3, e5);
  and and_4 (and_4_out, e1, e3);
  and and_5 (and_5_out, not_1_out, not_2_out, e3);
  and and_6 (and_6_out, not_1_out, e3, not_4_out);
  and and_7 (and_7_out, e1, not_3_out);
  or or_1 (s3, and_2_out, and_3_out, and_4_out);
  or or_2 (s4, and_5_out, and_6_out, and_7_out);

  assign s2 = e2;
endmodule
